// Logisim project ALU.circ as structural Verilog: 3 circuits, main circuit main
module main (
  input  A2,
  input  A1,
  input  [1:0] in_3,
  input  A0,
  input  B2,
  input  B1,
  input  B0
);

  wire alu_1_div_by_zero, alu_1_r0, alu_1_r1, alu_1_r2, alu_1_r3, alu_1_r4, alu_1_sign_flag, alu_1_zero_flag,
       n7448_1_p10, n7448_1_p11, n7448_1_p12, n7448_1_p13, n7448_1_p14, n7448_1_p15, n7448_1_p16;

  LED Div_by_Zero (.in(alu_1_div_by_zero));
  Alu alu_1 (
    .A2(A2), .A1(A1), .A0(A0), .B2(B2), .B1(B1), .B0(B0), .in_2(in_3), .R4(alu_1_r4), .R3(alu_1_r3),
    .Zero_flag(alu_1_zero_flag), .R2(alu_1_r2), .R1(alu_1_r1), .R0(alu_1_r0), .Sign_flag(alu_1_sign_flag),
    .Div_By_Zero(alu_1_div_by_zero));
  LED Sign_flag (.in(alu_1_sign_flag));
  LED Zero_Flag (.in(alu_1_zero_flag));
  // _7448 7448_1: pin names not known; wires that end beside it: alu_1_r1, alu_1_r2, 1'b1, 1'b1, 1'b1, alu_1_r3, alu_1_r0, 1'b0, 1'b1, n7448_1_p10, n7448_1_p11, n7448_1_p12, n7448_1_p13, n7448_1_p14, n7448_1_p15, n7448_1_p16
  _7_Segment_Display u_7_segment_display_1 (
    .g(n7448_1_p11), .f(n7448_1_p10), .a(n7448_1_p12), .b(n7448_1_p13), .e(n7448_1_p16), .d(n7448_1_p15),
    .c(n7448_1_p14), .dp(1'b0));
  _7_Segment_Display u_7_segment_display_2 (.g(alu_1_r4));  // open: f, a, b, e, d, c, dp
endmodule

module Alu (
  input  A2,
  input  [1:0] in_2,
  input  A1,
  input  A0,
  input  B2,
  input  B1,
  input  B0,
  output R4,
  output R3,
  output Zero_flag,
  output R2,
  output R1,
  output R0,
  output Sign_flag,
  output Div_By_Zero
);

  wire adder_subtractor_1_p8, adder_subtractor_1_p9, adder_subtractor_1_p10, adder_subtractor_1_p11,
       n6_in_6_out_1_c0, n6_in_6_out_1_c1, n6_in_6_out_1_c2, n6_in_6_out_1_c3, n6_in_6_out_1_sign_flag,
       remainder_1_r0, remainder_1_r1, remainder_1_sign;

  // Adder_Subtractor adder_subtractor_1: pin names not known; wires that end beside it: A2, A1, A0, B2, B1, B0, in_2[0], adder_subtractor_1_p8, adder_subtractor_1_p9, adder_subtractor_1_p10, adder_subtractor_1_p11
  _6_in_6_out u_6_in_6_out_1 (
    .A0(A0), .A1(A1), .A2(A2), .B0(B0), .B1(B1), .B2(B2), .Sign_flag(n6_in_6_out_1_sign_flag),
    .C0(n6_in_6_out_1_c0), .C1(n6_in_6_out_1_c1), .C2(n6_in_6_out_1_c2), .C3(n6_in_6_out_1_c3));  // open: Zero_flag
  Remainder remainder_1 (
    .A2(A2), .A1(A1), .A0(A0), .B2(B2), .B1(B1), .B0(B0), .R0(remainder_1_r0), .R1(remainder_1_r1),
    .Sign(remainder_1_sign));  // open: Div_by_Zero_flag, Zero_flag
  Div_By_Zero_flag div_by_zero_flag_1 (.B0(B1), .B1(B0), .in_3(in_2), .Div_by_zero(Div_By_Zero));
  Multiplexer #(.select(2), .enable("false")) multiplexer_1 (
    .in0(adder_subtractor_1_p8), .in1(adder_subtractor_1_p8), .in2(n6_in_6_out_1_sign_flag),
    .in3(remainder_1_sign), .out(R4), .sel(in_2));
  Multiplexer #(.select(2), .enable("false")) multiplexer_2 (
    .in0(1'b0), .in1(1'b0), .in2(n6_in_6_out_1_c3), .in3(1'b0), .out(R3), .sel(in_2));
  Multiplexer #(.select(2), .enable("false")) multiplexer_3 (
    .in0(adder_subtractor_1_p11), .in1(adder_subtractor_1_p11), .in2(n6_in_6_out_1_c2), .in3(1'b0), .out(R2),
    .sel(in_2));
  Multiplexer #(.select(2), .enable("false")) multiplexer_4 (
    .in0(adder_subtractor_1_p10), .in1(adder_subtractor_1_p10), .in2(n6_in_6_out_1_c1), .in3(remainder_1_r1),
    .out(R1), .sel(in_2));
  Multiplexer #(.select(2), .enable("false")) multiplexer_5 (
    .in0(adder_subtractor_1_p9), .in1(adder_subtractor_1_p9), .in2(n6_in_6_out_1_c0), .in3(remainder_1_r0),
    .out(R0), .sel(in_2));
  nor nor_1 (Zero_flag, R4, R3, R2, R1, R0);

  assign Sign_flag = R4;
endmodule

module Div_By_Zero_flag (
  input  B0,
  input  B1,
  input  [1:0] in_3,
  output Div_by_zero
);

  wire and_1_out, not_1_out, not_2_out;

  and and_1 (and_1_out, in_3[0], in_3[1]);
  not not_1 (not_1_out, B1);
  not not_2 (not_2_out, B0);
  and and_2 (Div_by_zero, not_2_out, not_1_out, and_1_out);
endmodule
