// Logisim project MULTIPLIER.circ as structural Verilog: 2 circuits, main circuit main
module main (
  input  A0,
  input  A1,
  input  A2,
  input  B0,
  input  B1,
  input  B2
);

  wire n6_in_6_out_1_c0, n6_in_6_out_1_c1, n6_in_6_out_1_c2, n6_in_6_out_1_c3, n6_in_6_out_1_sign_flag,
       n6_in_6_out_1_zero_flag, n7448_1_p10, n7448_1_p11, n7448_1_p12, n7448_1_p13, n7448_1_p14, n7448_1_p15,
       n7448_1_p16;

  LED Zero_flag (.in(n6_in_6_out_1_zero_flag));
  _6_in_6_out u_6_in_6_out_1 (
    .A0(A0), .A1(A1), .A2(A2), .B0(B0), .B1(B1), .B2(B2), .Zero_flag(n6_in_6_out_1_zero_flag),
    .Sign_flag(n6_in_6_out_1_sign_flag), .C0(n6_in_6_out_1_c0), .C1(n6_in_6_out_1_c1), .C2(n6_in_6_out_1_c2),
    .C3(n6_in_6_out_1_c3));
  LED Sign_flag (.in(n6_in_6_out_1_sign_flag));
  // _7448 7448_1: pin names not known; wires that end beside it: n6_in_6_out_1_c1, n6_in_6_out_1_c2, 1'b1, 1'b1, 1'b1, n6_in_6_out_1_c3, n6_in_6_out_1_c0, 1'b0, 1'b1, n7448_1_p10, n7448_1_p11, n7448_1_p12, n7448_1_p13, n7448_1_p14, n7448_1_p15, n7448_1_p16
  _7_Segment_Display u_7_segment_display_1 (
    .g(n7448_1_p11), .f(n7448_1_p10), .a(n7448_1_p12), .b(n7448_1_p13), .e(n7448_1_p16), .d(n7448_1_p15),
    .c(n7448_1_p14));  // open: dp
  _7_Segment_Display u_7_segment_display_2 (.g(n6_in_6_out_1_sign_flag));  // open: f, a, b, e, d, c, dp
endmodule

// Multiplier
module _6_in_6_out (
  input  A0,
  input  A1,
  input  A2,
  input  B0,
  input  B1,
  input  B2,
  output C0,
  output Zero_flag,
  output C1,
  output C2,
  output C3,
  output Sign_flag
);

  wire and_1_out, and_2_out, nand_1_out, or_1_out, xor_2_out;

  and and_1 (and_1_out, A0, B1);
  and and_2 (and_2_out, A1, B0);
  xor xor_1 (C1, and_1_out, and_2_out);
  nand nand_1 (nand_1_out, A0, B0);
  xor xor_2 (xor_2_out, A2, B2);
  and and_3 (C0, A0, B0);
  and and_4 (C2, A1, B1, nand_1_out);
  and and_5 (C3, A0, A1, B0, B1);
  or or_1 (or_1_out, C0, C1, C2, C3);
  not not_1 (Zero_flag, or_1_out);
  and and_6 (Sign_flag, xor_2_out, or_1_out);
endmodule
