// Logisim project Remainder.circ as structural Verilog
module Remainder (
  input  A2,
  input  A1,
  input  A0,
  input  B2,
  input  B1,
  input  B0,
  output Sign,
  output Div_by_Zero_flag,
  output Zero_flag,
  output R1,
  output R0
);

  wire and_2_out, div_by_zero_1_b0_2, div_by_zero_1_b1_2, nand_1_out, not_1_out, or_1_out, or_2_out;

  or or_1 (or_1_out, A1, A0);
  and and_1 (Sign, or_1_out, or_2_out, A2);
  Div_by_zero div_by_zero_1 (
    .B1(B1), .B0(B0), .Div_by_zero(Div_by_Zero_flag), .B1_2(div_by_zero_1_b1_2), .B0_2(div_by_zero_1_b0_2));
  or or_2 (or_2_out, R1, R0);
  not not_1 (not_1_out, A0);
  and and_2 (and_2_out, A0, div_by_zero_1_b1_2);
  and and_3 (R1, div_by_zero_1_b0_2, A1, div_by_zero_1_b1_2, not_1_out);
  nand nand_1 (nand_1_out, A1, div_by_zero_1_b0_2);
  and and_4 (R0, and_2_out, nand_1_out);
  nor nor_1 (Zero_flag, R1, R0);
endmodule

module Remainder_with_decoder (
  input  A2,
  input  A1,
  input  A0,
  input  B2,
  input  B1,
  input  B0
);

  wire n7448_1_p10, n7448_1_p11, n7448_1_p12, n7448_1_p13, n7448_1_p14, n7448_1_p15, n7448_1_p16,
       n7448_2_p10, remainder_1_div_by_zero_flag, remainder_1_r0, remainder_1_r1, remainder_1_sign,
       remainder_1_zero_flag;

  LED Div_by_zero_flag (.in(remainder_1_div_by_zero_flag));
  Remainder remainder_1 (
    .A2(A2), .A1(A1), .A0(A0), .B2(B2), .B1(B1), .B0(B0), .Div_by_Zero_flag(remainder_1_div_by_zero_flag),
    .R0(remainder_1_r0), .R1(remainder_1_r1), .Sign(remainder_1_sign), .Zero_flag(remainder_1_zero_flag));
  LED Zero_Flag (.in(remainder_1_zero_flag));
  // _7448 7448_1: pin names not known; wires that end beside it: remainder_1_r1, 1'b0, 1'b1, 1'b1, 1'b1, 1'b0, remainder_1_r0, 1'b0, 1'b1, n7448_1_p10, n7448_1_p11, n7448_1_p12, n7448_1_p13, n7448_1_p14, n7448_1_p15, n7448_1_p16
  // _7448 7448_2: pin names not known; wires that end beside it: 1'b0, 1'b0, 1'b1, 1'b1, 1'b1, remainder_1_sign, 1'b0, 1'b0, 1'b1, n7448_2_p10
  _7_Segment_Display u_7_segment_display_1 (
    .g(n7448_1_p11), .f(n7448_1_p10), .a(n7448_1_p12), .b(n7448_1_p13), .e(n7448_1_p16), .d(n7448_1_p15),
    .c(n7448_1_p14), .dp(1'b0));
  _7_Segment_Display u_7_segment_display_2 (.g(n7448_2_p10));  // open: f, a, b, e, d, c, dp
endmodule

module Div_by_zero (
  input  B1,
  input  B0,
  output Div_by_zero,
  output B1_2,
  output B0_2
);

  wire not_1_out, not_2_out;

  not not_1 (not_1_out, B1);
  not not_2 (not_2_out, B0);
  and and_1 (Div_by_zero, not_1_out, not_2_out);

  assign B0_2 = B0;
  assign B1_2 = B1;
endmodule
