// Logisim project signed adder_subtractor optimized.circ as structural Verilog: 3 circuits, main circuit Adder/Subtractor
module Adder_Subtractor (
  input  A2,
  input  A1,
  input  A0,
  input  B2,
  input  B1,
  input  B0,
  input  Operation,
  output _1,
  output _2,
  output _3,
  output _4
);

  wire n2_complemnet_1_a0_comp, n2_complemnet_1_a1_comp, n2_complemnet_1_a2_comp, n2_complemnet_1_sign,
       n2_complemnet_2_a0_comp, n2_complemnet_2_a1_comp, n2_complemnet_2_a2_comp, n2_complemnet_2_sign,
       n4_bit_fa_1_s0, n4_bit_fa_1_s1, n4_bit_fa_1_s2, n4_bit_fa_1_s3, n7448_1_p10, n7448_1_p11, n7448_1_p12,
       n7448_1_p13, n7448_1_p14, n7448_1_p15, n7448_1_p16, nor_1_out, xor_1_out;

  xor xor_1 (xor_1_out, Operation, B2);
  _2_complemnet u_2_complemnet_1 (
    .A2(1'b0), .A1(A1), .A0(A0), .AS(A2), .A2_comp(n2_complemnet_1_a2_comp),
    .A1_comp(n2_complemnet_1_a1_comp), .A0_comp(n2_complemnet_1_a0_comp), .sign(n2_complemnet_1_sign));
  _2_complemnet u_2_complemnet_2 (
    .A2(1'b0), .A1(B1), .A0(B0), .AS(xor_1_out), .A2_comp(n2_complemnet_2_a2_comp),
    .A1_comp(n2_complemnet_2_a1_comp), .A0_comp(n2_complemnet_2_a0_comp), .sign(n2_complemnet_2_sign));
  _4_bit_FA u_4_bit_fa_1 (
    .A0(n2_complemnet_1_a0_comp), .B0(n2_complemnet_2_a0_comp), .A1(n2_complemnet_1_a1_comp),
    .B1(n2_complemnet_2_a1_comp), .A2(n2_complemnet_1_a2_comp), .B2(n2_complemnet_2_a2_comp),
    .A3(n2_complemnet_1_sign), .B3(n2_complemnet_2_sign), .Cin(1'b0), .S0(n4_bit_fa_1_s0),
    .S1(n4_bit_fa_1_s1), .S2(n4_bit_fa_1_s2), .S3(n4_bit_fa_1_s3));  // open: Cout
  _2_complemnet u_2_complemnet_3 (
    .A2(n4_bit_fa_1_s2), .A1(n4_bit_fa_1_s1), .A0(n4_bit_fa_1_s0), .AS(n4_bit_fa_1_s3), .A2_comp(_4),
    .A1_comp(_3), .A0_comp(_2), .sign(_1));
  LED Sign_flag (.in(_1));
  // _7448 7448_1: pin names not known; wires that end beside it: _3, _4, 1'b1, 1'b1, 1'b1, 1'b0, _2, 1'b0, 1'b1, n7448_1_p10, n7448_1_p11, n7448_1_p12, n7448_1_p13, n7448_1_p14, n7448_1_p15, n7448_1_p16
  nor nor_1 (nor_1_out, _2, _3, _4, _4);
  LED Zero_flag (.in(nor_1_out));
  _7_Segment_Display u_7_segment_display_1 (.g(_1));  // open: f, a, b, e, d, c, dp
  _7_Segment_Display u_7_segment_display_2 (
    .g(n7448_1_p11), .f(n7448_1_p10), .a(n7448_1_p12), .b(n7448_1_p13), .e(n7448_1_p16), .d(n7448_1_p15),
    .c(n7448_1_p14));  // open: dp

  // Notes on the sheet:
  //   7-Segment-Decoder
endmodule

module _4_bit_FA (
  input  Cin,
  input  A0,
  input  B0,
  input  A1,
  input  B1,
  input  A2,
  input  B2,
  input  A3,
  input  B3,
  output S0,
  output S1,
  output S2,
  output S3,
  output Cout
);

  wire adder_1_cout, adder_2_cout, adder_3_cout;

  Adder #(.width(1)) adder_1 (.a(A0), .b(B0), .out(S0), .cin(Cin), .cout(adder_1_cout));
  Adder #(.width(1)) adder_2 (.a(A1), .b(B1), .out(S1), .cin(adder_1_cout), .cout(adder_2_cout));
  Adder #(.width(1)) adder_3 (.a(A2), .b(B2), .out(S2), .cin(adder_2_cout), .cout(adder_3_cout));
  Adder #(.width(1)) adder_4 (.a(A3), .b(B3), .out(S3), .cin(adder_3_cout), .cout(Cout));
endmodule

module _2_complemnet (
  input  A2,
  input  A1,
  input  A0,
  input  AS,
  output A1_comp,
  output A0_comp,
  output sign,
  output A2_comp
);

  wire and_1_out, and_2_out, or_1_out, or_2_out;

  and and_1 (and_1_out, AS, or_1_out);
  xor xor_1 (A2_comp, A2, and_1_out);
  or or_1 (or_1_out, A1, A0);
  and and_2 (and_2_out, A0, AS);
  xor xor_2 (A1_comp, A1, and_2_out);
  or or_2 (or_2_out, A0, A1, A2);
  and and_3 (sign, or_2_out, AS);

  assign A0_comp = A0;
endmodule
